// Logisim project Main.circ as structural Verilog: 4 circuits, main circuit main
module main (
);

  wire controlunit_1_alusub, controlunit_1_alutoac, controlunit_1_alutopc, controlunit_1_alutorr,
       controlunit_1_alutosp, controlunit_1_ar_sp_sel, controlunit_1_cuclk, controlunit_1_rrclr,
       registerbank_1_acz, registerbank_1_spz;
  wire [1:0] controlunit_1_aluinsel;
  wire [2:0] controlunit_1_dbsel, controlunit_1_reglds;
  wire [9:0] registerbank_1_irtocu;

  controlUnit controlunit_1 (
    .ACZ(registerbank_1_acz), .SPZ(registerbank_1_spz), .IR(registerbank_1_irtocu),
    .DBSel(controlunit_1_dbsel), .AR_SP_Sel(controlunit_1_ar_sp_sel), .regLds(controlunit_1_reglds),
    .RRCLR(controlunit_1_rrclr), .ALUtoPC(controlunit_1_alutopc), .ALUtoSP(controlunit_1_alutosp),
    .ALUtoRR(controlunit_1_alutorr), .ALUtoAC(controlunit_1_alutoac), .ALUSub(controlunit_1_alusub),
    .ALUinSel(controlunit_1_aluinsel), .CUClk(controlunit_1_cuclk));
  registerBank registerbank_1 (
    .AR_SPSel(controlunit_1_ar_sp_sel), .ALUINSel(controlunit_1_aluinsel), .DBSel(controlunit_1_dbsel),
    .RBClk(controlunit_1_cuclk), .regLdS(controlunit_1_reglds), .RRClr(controlunit_1_rrclr),
    .ALUtoPC(controlunit_1_alutopc), .ALUtoSP(controlunit_1_alutosp), .SPZ(registerbank_1_spz),
    .ALUsub(controlunit_1_alusub), .ALUtoRR(controlunit_1_alutorr), .ALUtoAC(controlunit_1_alutoac),
    .ACZ(registerbank_1_acz), .IRtoCU(registerbank_1_irtocu));
endmodule

module registerBank (
  input  AR_SPSel,
  input  ALUtoPC,
  input  ALUtoSP,
  input  ALUsub,
  input  ALUtoRR,
  input  RRClr,
  input  [1:0] ALUINSel,
  input  ALUtoAC,
  input  RBClk,
  input  [2:0] regLdS,
  input  [2:0] DBSel,
  output SPZ,
  output ACZ,
  output [9:0] IRtoCU
);

  wire decoder_1_out0, decoder_1_out1, decoder_1_out2, decoder_1_out3, decoder_1_out4, decoder_1_out5,
       decoder_1_out6, not_1_out;
  wire [6:0] AR_q, PC_q, SP_q;
  wire [9:0] AC_q, alu_1_input, bit_extender_1_out, bit_extender_2_out, multiplexer_2_out, multiplexer_3_out,
       multiplexer_4_out, multiplexer_5_out, multiplexer_16_out, ram_1_data, RR_q, undriven;

  ALU alu_1 (.Input(alu_1_input), .Sub(ALUsub), .Output(undriven));
  Multiplexer #(.select(2), .width(10), .enable("false")) multiplexer_1 (
    .in0(AC_q), .in1(RR_q), .in2(bit_extender_1_out), .in3(bit_extender_2_out), .out(alu_1_input),
    .sel(ALUINSel));
  Decoder #(.select(3), .enable("false")) decoder_1 (
    .out0(decoder_1_out0), .out1(decoder_1_out1), .out2(decoder_1_out2), .out3(decoder_1_out3),
    .out4(decoder_1_out4), .out5(decoder_1_out5), .out6(decoder_1_out6), .sel(regLdS));  // open: out7
  Multiplexer #(.width(10), .enable("false")) multiplexer_2 (
    .in0(multiplexer_16_out), .in1(undriven), .out(multiplexer_2_out), .sel(ALUtoPC));
  Multiplexer #(.width(10), .enable("false")) multiplexer_3 (
    .in0(multiplexer_16_out), .in1(undriven), .out(multiplexer_3_out), .sel(ALUtoSP));
  Multiplexer #(.width(10), .enable("false")) multiplexer_4 (
    .in0(multiplexer_16_out), .in1(undriven), .out(multiplexer_4_out), .sel(ALUtoRR));
  Multiplexer #(.width(10), .enable("false")) multiplexer_5 (
    .in0(multiplexer_16_out), .in1(undriven), .out(multiplexer_5_out), .sel(ALUtoAC));
  assign bit_extender_1_out = {{3{1'b0}}, SP_q};  // Bit_Extender bit_extender_1
  Register #(.width(7)) AR (.D(multiplexer_16_out[6:0]), .en(decoder_1_out0), .Q(AR_q), .clk(RBClk));  // open: clr
  assign bit_extender_2_out = {{3{1'b0}}, PC_q};  // Bit_Extender bit_extender_2
  Register #(.width(7)) PC (.D(multiplexer_2_out[6:0]), .en(decoder_1_out1), .Q(PC_q), .clk(RBClk));  // open: clr
  Register #(.width(7)) SP (.D(multiplexer_3_out[6:0]), .en(decoder_1_out2), .Q(SP_q), .clk(RBClk));  // open: clr
  Register #(.width(10)) RR (.D(multiplexer_4_out), .en(decoder_1_out3), .Q(RR_q), .clk(RBClk), .clr(RRClr));
  Register #(.width(10)) AC (.D(multiplexer_5_out), .en(decoder_1_out4), .Q(AC_q), .clk(RBClk));  // open: clr
  Register #(.width(10)) IR (.D(multiplexer_16_out), .en(decoder_1_out5), .Q(IRtoCU), .clk(RBClk));  // open: clr
  not not_1 (not_1_out, decoder_1_out6);
  RAM #(.addrWidth(7), .dataWidth(10), .bus("separate")) ram_1 (
    .addr(SP_q), .din(multiplexer_16_out), .data(ram_1_data), .str(decoder_1_out6), .sel(1'b1), .clk(RBClk),
    .ld(not_1_out), .clr(1'b0));
  Multiplexer #(.width(7), .enable("false")) multiplexer_6 (.in0(AR_q), .in1(SP_q), .out(SP_q), .sel(AR_SPSel));
  Multiplexer #(.select(3), .enable("false")) multiplexer_7 (
    .in0(1'b0), .in1(ram_1_data[9]), .in2(IRtoCU[9]), .in3(AC_q[9]), .in4(RR_q[9]), .in5(1'b0), .in6(1'b0),
    .in7(1'b0), .out(multiplexer_16_out[9]), .sel(DBSel));
  Multiplexer #(.select(3), .enable("false")) multiplexer_8 (
    .in0(1'b0), .in1(ram_1_data[8]), .in2(IRtoCU[8]), .in3(AC_q[8]), .in4(RR_q[8]), .in5(1'b0), .in6(1'b0),
    .in7(1'b0), .out(multiplexer_16_out[8]), .sel(DBSel));
  Multiplexer #(.select(3), .enable("false")) multiplexer_9 (
    .in0(1'b0), .in1(ram_1_data[7]), .in2(IRtoCU[7]), .in3(AC_q[7]), .in4(RR_q[7]), .in5(1'b0), .in6(1'b0),
    .in7(1'b0), .out(multiplexer_16_out[7]), .sel(DBSel));
  Multiplexer #(.select(3), .enable("false")) multiplexer_10 (
    .in0(1'b0), .in1(ram_1_data[6]), .in2(IRtoCU[6]), .in3(AC_q[6]), .in4(RR_q[6]), .in5(SP_q[6]),
    .in6(PC_q[6]), .in7(AR_q[6]), .out(multiplexer_16_out[6]), .sel(DBSel));
  Multiplexer #(.select(3), .enable("false")) multiplexer_11 (
    .in0(1'b0), .in1(ram_1_data[5]), .in2(IRtoCU[5]), .in3(AC_q[5]), .in4(RR_q[5]), .in5(SP_q[5]),
    .in6(PC_q[5]), .in7(AR_q[5]), .out(multiplexer_16_out[5]), .sel(DBSel));
  Multiplexer #(.select(3), .enable("false")) multiplexer_12 (
    .in0(1'b0), .in1(ram_1_data[4]), .in2(IRtoCU[4]), .in3(AC_q[4]), .in4(RR_q[4]), .in5(SP_q[4]),
    .in6(PC_q[4]), .in7(AR_q[4]), .out(multiplexer_16_out[4]), .sel(DBSel));
  Multiplexer #(.select(3), .enable("false")) multiplexer_13 (
    .in0(1'b0), .in1(ram_1_data[3]), .in2(IRtoCU[3]), .in3(AC_q[3]), .in4(RR_q[3]), .in5(SP_q[3]),
    .in6(PC_q[3]), .in7(AR_q[3]), .out(multiplexer_16_out[3]), .sel(DBSel));
  Multiplexer #(.select(3), .enable("false")) multiplexer_14 (
    .in0(1'b0), .in1(ram_1_data[2]), .in2(IRtoCU[2]), .in3(AC_q[2]), .in4(RR_q[2]), .in5(SP_q[2]),
    .in6(PC_q[2]), .in7(AR_q[2]), .out(multiplexer_16_out[2]), .sel(DBSel));
  Multiplexer #(.select(3), .enable("false")) multiplexer_15 (
    .in0(1'b0), .in1(ram_1_data[1]), .in2(IRtoCU[1]), .in3(AC_q[1]), .in4(RR_q[1]), .in5(SP_q[1]),
    .in6(PC_q[1]), .in7(AR_q[1]), .out(multiplexer_16_out[1]), .sel(DBSel));
  Multiplexer #(.select(3), .enable("false")) multiplexer_16 (
    .in0(1'b0), .in1(ram_1_data[0]), .in2(IRtoCU[0]), .in3(AC_q[0]), .in4(RR_q[0]), .in5(SP_q[0]),
    .in6(PC_q[0]), .in7(AR_q[0]), .out(multiplexer_16_out[0]), .sel(DBSel));
  nand nand_1 (SPZ, SP_q[0], SP_q[1], SP_q[2], SP_q[3], SP_q[4], SP_q[5], SP_q[6]);
  nand nand_2 (ACZ, AC_q[0], AC_q[1], AC_q[2], AC_q[3], AC_q[4], AC_q[5], AC_q[6], AC_q[7], AC_q[8], AC_q[9]);

  // Notes on the sheet:
  //   DB sel = 7
  //   DB sel = 6
  //   DB sel = 5
  //   DB sel = 4
  //   DB sel = 3
  //   DB sel = 2
  //   DB sel = 1
endmodule

module controlUnit (
  input  ACZ,
  input  SPZ,
  input  [9:0] IR,
  output [2:0] DBSel,
  output AR_SP_Sel,
  output [2:0] regLds,
  output RRCLR,
  output ALUtoPC,
  output ALUtoSP,
  output ALUtoRR,
  output ALUtoAC,
  output ALUSub,
  output [1:0] ALUinSel,
  output CUClk
);

  wire and_1_out, and_2_out, and_3_out, and_4_out, and_5_out, and_6_out, and_7_out, and_8_out,
       decoder_1_out0, decoder_1_out1, decoder_1_out2, decoder_1_out3, decoder_1_out4, decoder_1_out5,
       decoder_1_out6, decoder_1_out7, decoder_2_out0, decoder_2_out1, decoder_2_out2, decoder_2_out3,
       decoder_2_out4, not_1_out, not_2_out, or_1_out;
  wire [2:0] counter_q;
  wire [3:0] priority_encoder_1_out;
  wire [4:0] multiplexer_1_out;
  wire [9:8] rom_1_data;

  not not_1 (not_1_out, SPZ);
  Decoder #(.select(3), .enable("false")) decoder_1 (
    .out0(decoder_1_out0), .out1(decoder_1_out1), .out2(decoder_1_out2), .out3(decoder_1_out3),
    .out4(decoder_1_out4), .out5(decoder_1_out5), .out6(decoder_1_out6), .out7(decoder_1_out7), .sel(IR[9:7]));
  Counter #(.width(3), .max('h7)) counter (.Q(counter_q), .clk(CUClk), .clr(or_1_out));  // open: load, D, count, carry
  Clock clock_1 (.out(CUClk));
  Decoder #(.select(3)) decoder_2 (
    .out0(decoder_2_out0), .out1(decoder_2_out1), .out2(decoder_2_out2), .out3(decoder_2_out3),
    .out4(decoder_2_out4), .sel(counter_q), .en(not_2_out));  // open: out5, out6, out7
  and and_1 (and_1_out, decoder_1_out0, decoder_2_out3);
  and and_2 (and_2_out, decoder_1_out1, decoder_2_out3);
  and and_3 (and_3_out, decoder_1_out2, ACZ, decoder_2_out3);
  and and_4 (and_4_out, decoder_1_out3, decoder_2_out3);
  and and_5 (and_5_out, decoder_1_out4, not_1_out, decoder_2_out3);
  and and_6 (and_6_out, decoder_2_out3, ACZ, decoder_1_out5);
  and and_7 (and_7_out, decoder_2_out3, decoder_1_out6);
  and and_8 (and_8_out, decoder_1_out1, decoder_2_out4);
  not not_2 (not_2_out, decoder_1_out7);
  or or_1 (or_1_out, and_7_out, and_6_out, and_5_out, and_4_out, and_3_out, and_8_out, and_1_out);
  Priority_Encoder #(.select(4)) priority_encoder_1 (
    .in0(decoder_2_out0), .in1(decoder_2_out1), .in2(decoder_2_out2), .in3(and_1_out), .in4(and_2_out),
    .in5(and_8_out), .in6(and_3_out), .in7(and_4_out), .in8(and_5_out), .in9(and_6_out), .in10(and_7_out),
    .out(priority_encoder_1_out), .en_in(1'b1));  // open: in11, in12, in13, in14, in15, gs, en_out
  Multiplexer #(.select(4), .width(5), .enable("false")) multiplexer_1 (
    .in0({5{1'b0}}), .in1(5'b00001), .in2(5'b00010), .in3(5'b00011), .in4(5'b00100), .in5(5'b00101),
    .in6(5'b00110), .in7(5'b00111), .in8(5'b01000), .in9(5'b01001), .in10(5'b01010), .in11(5'b01011),
    .out(multiplexer_1_out), .sel(priority_encoder_1_out));  // open: in12, in13, in14, in15
  ROM #(.addrWidth(5), .dataWidth(13)) rom_1 (
    .addr(multiplexer_1_out), .data({ALUinSel, ALUSub, rom_1_data, RRCLR, regLds, AR_SP_Sel, DBSel}),
    .sel(1'b1));
  Decoder #(.select(2), .enable("false")) decoder_3 (
    .out0(ALUtoPC), .out1(ALUtoSP), .out2(ALUtoRR), .out3(ALUtoAC), .sel(rom_1_data));

  // Notes on the sheet:
  //   contents of rom_1 (hex, n*v repeats v):
  //   1800 543 1c80 f8e a 1b80 11 1c 440 440 20
endmodule

module ALU (
  input  [9:0] Output,
  input  Sub,
  output [9:0] Input
);

  wire [9:0] multiplexer_1_out;

  Multiplexer #(.width(10), .enable("false")) multiplexer_1 (
    .in0(10'h1), .in1({10{1'b1}}), .out(multiplexer_1_out), .sel(Sub));
  Adder #(.width(10)) adder_1 (.a(Input), .b(multiplexer_1_out), .out(Output));  // open: cin, cout
endmodule
